# Fritzing sketch Circuitos (saved by Fritzing 0.9.3b)
circuit board: 7.52641cm x 4.21055cm
breadboards: 1

parts:
  HLK-PM1 = HLK-PM01
  J1 = Camdenboss CTB0158-2 [part_number=CTB0158-2 package=THT]
  J2 = Dagu DGServo 9g header (male) [package=THT]
  Infrarojo = Camdenboss CTB0158-10 [part_number=CTB0158-10 package=THT]
  10k = Resistor [tolerance=±5% resistance=10 package=THT]
  220 = Resistor [tolerance=±5% resistance=220 package=THT]

nets (from the pcb view):
  N1: HLK-PM1.AC#0, J1.pin2
  N2: HLK-PM1.AC#1, J1.pin1
  N3: HLK-PM1.-Vo, J2.pulse, Infrarojo.pin1, Infrarojo.pin8, 10k.Pin_0, 220.Pin_1
  N4: HLK-PM1.+Vo, J2.Vcc, Infrarojo.pin2, Infrarojo.pin5, Infrarojo.pin6, Infrarojo.pin7
  N5: J2.gnd, Infrarojo.pin4
  N6: Infrarojo.pin3, Infrarojo.pin9, 10k.Pin_1
  N7: Infrarojo.pin10, 220.Pin_0
